# Fritzing sketch Schematics (saved by Fritzing 0.9.3b)
circuit board: 8.46667cm x 5.64444cm

parts:
  Componente1 = Arduino Nano (Rev3.0)
  BAT1 = BC9VPC [package=bc9vpc]
  Componente2 = Barometric Pressure Sensor - BMP180 Breakout (GY-68)
  Componente3 = InvenSense MPU6050
  microSD1 = MicroSD Card Module
  J1 = Piezo Speaker

nets:
  GND: Componente1.GND, BAT1.V-, Componente2.GND, Componente3.GND, J1.pin1
  N1: Componente1.D6, J1.pin2
  N2: Componente1.D10, microSD1.CS
  N3: Componente1.D11/MOSI, microSD1.MOSI
  N4: Componente1.D12/MISO, microSD1.MISO
  N5: Componente1.VIN, BAT1.V+
  5V: Componente1.5V, microSD1.VCC
  N6: Componente1.A4, Componente2.SCL, Componente3.SCL
  N7: Componente1.A3, Componente2.SDA, Componente3.SDA
  VCC: Componente1.3V3, Componente2.VCC, Componente3.VCC
  N8: Componente1.D13/SCK, microSD1.SCK
